# Fritzing sketch Sketch (saved by Fritzing 0.9.3b)
breadboards: 1

parts:
  LCD1 = LCD screen  # not connected
  Part1 = BME280 Breakout  # not connected
  U1 = NodeMCU V3.0
  Q1 = Basic FET P-Channel [package="TO220 [THT]"]  # not connected
  D1 = Rectifier Diode [part_number=1N4001 package="300 mil [THT]"]  # not connected
  D2 = Rectifier Diode [part_number=1N4001 package="300 mil [THT]"]  # not connected
  S1 = Toggle Switch [package=THT]  # not connected
  VCC1 = Battery  # not connected

nets:
  N1: U1.GND#6, U1.GND#13, U1.GND#16, U1.GND#33

custom parts:
  NodeMCU V3.0: ESP8266 based NodeMCU
